# Fritzing sketch MycoFarmV1 (saved by Fritzing 0.9.5d)
breadboards: 2

parts:
  Part1 = Arduino Uno (Rev3) - ICSP
  DHT1 = DHT11 Humitidy and Temperature Sensor
  Part2 = Adafruit CCS811
  U1 = 4RelayModule
  Raspberry_Pi_1 = Raspberry Pi 3 [part_number=RPI-3-V1.2]  # not connected
  Q1 = PNP-Transistor [part_number=2N3906 package="TO92 [THT]"]
  Q2 = NPN-Transistor [part_number=2N3904 package="TO92 [THT]"]
  R1 = Resistor [tolerance=±5% resistance=1k package="2512 [SMD]"]
  12VDC = 2.1mm Barrel Jack with Terminal Block
  5VDC2 = 2.1mm Barrel Jack with Terminal Block  # not connected
  5VDC1 = 2.1mm Barrel Jack with Terminal Block  # not connected
  24VAC = 2.1mm Barrel Jack with Terminal Block
  24VAC_Irrigation_Solenoid = Solenoid
  R2 = Resistor [tolerance=±5% resistance=1k package="2512 [SMD]"]
  12V_FAE_Fan = DC Motor
  o1 = Module display OLED I2C 128x64 SSD1306 [package=THT]
  Grow_Lamp_5VDC = Incandescent light bulb small [package="bulb sm"]  # not connected
  Pad_Heater_?VDC = Peltier Element  # not connected

nets:
  N1: Part1.A4/SDA, Part2.SDA, o1.SDA
  N2: Part1.A5/SCL, Part2.SCL, o1.SCL
  N3: Part1.D8, DHT1.VDD
  N4: Part1.D10_PWM/SS, U1.IN4
  N5: Part1.D11_PWM/MOSI, U1.IN3
  N6: Part1.D12/MISO, U1.IN2
  N7: Part1.D13/SCK, U1.IN1
  N8: Part1.D6_PWM, R2.Pin_1
  VCC: Part1.5V, DHT1.DATA, Part2.VIN, U1.VCC, o1.VCC
  GND: Part1.GND, DHT1.NULL, Part2.GND, Part2.!WAKE, U1.GND, 12VDC.NEG, 12V_FAE_Fan.pin_1, o1.GND
  N9: U1.NC1, 24VAC.POS
  N10: U1.NO1, 24VAC_Irrigation_Solenoid.pin2
  N11: Q1.E, 12VDC.POS
  N12: Q1.B, R1.Pin_0
  N13: Q1.C, 12V_FAE_Fan.pin_2
  N14: Q2.B, R2.Pin_0
  N15: Q2.C, R1.Pin_1
  N16: 24VAC.NEG, 24VAC_Irrigation_Solenoid.pin1

notes:
  Grow Lamp 5VDC
  Pad Heater ??? DC
  Per Tub
  Master Controller
  DHT11/22 T&H Sensor
  CCS811 eCO2 Sensor

custom parts:
  DHT11 Humitidy and Temperature Sensor: DHT11 Humidity and Temperature Sensor
  4RelayModule: 4 relay arduino module SONGLE SRD05VDC-SL-C
  Module display OLED I2C 128x64 SSD1306: Ecran OLED I2C SSD163 de 128x64 avec connexion I2C
